// Logisim project ctrs.circ as structural Verilog: 3 circuits, main circuit main
module main (
);

  wire clock_1_out, fff4_1_o, fff4_1_q1, fff4_1_q2, fff4_1_q3, fff4_1_q6, fff4_1_q9, fff4_1_q18, fff4_1_q27,
       fff4_1_q54, fff4_2_o, fff4_2_q1, fff4_2_q2, fff4_2_q3, fff4_2_q6, fff4_2_q9, fff4_2_q18, nand_1_out,
       nand_2_out;

  Clock clock_1 (.out(clock_1_out));
  nand nand_1 (nand_1_out, fff4_1_q54, fff4_1_q6);
  nand nand_2 (nand_2_out, fff4_2_q18, fff4_2_q6);
  LED led_1 (.in(fff4_1_q1));
  fff4 fff4_1 (
    .I(clock_1_out), .R(nand_1_out), .Q1(fff4_1_q1), .Q2(fff4_1_q2), .Q3(fff4_1_q3), .Q6(fff4_1_q6),
    .Q9(fff4_1_q9), .Q18(fff4_1_q18), .Q27(fff4_1_q27), .Q54(fff4_1_q54), .O(fff4_1_o));
  LED led_2 (.in(fff4_1_q2));
  LED led_3 (.in(fff4_1_q3));
  LED led_4 (.in(fff4_1_q6));
  LED led_5 (.in(fff4_1_q9));
  LED led_6 (.in(fff4_1_q18));
  LED led_7 (.in(fff4_1_q27));
  LED led_8 (.in(fff4_1_q54));
  LED led_9 (.in(fff4_1_o));
  LED led_10 (.in(fff4_2_q1));
  fff4 fff4_2 (
    .I(fff4_1_o), .R(nand_2_out), .Q1(fff4_2_q1), .Q2(fff4_2_q2), .Q3(fff4_2_q3), .Q6(fff4_2_q6),
    .Q9(fff4_2_q9), .Q18(fff4_2_q18), .O(fff4_2_o));  // open: Q27, Q54
  LED led_11 (.in(fff4_2_q2));
  LED led_12 (.in(fff4_2_q3));
  LED led_13 (.in(fff4_2_q6));
  LED led_14 (.in(fff4_2_q9));
  LED led_15 (.in(fff4_2_q18));
  LED led_16 (.in(fff4_2_o));
endmodule

module fff (
  input  I,
  input  R,
  output Q1,
  output Q0,
  output O
);

  wire n7474_1_pin4, n7474_1_pin10;

  _7402 #(.ShowInternalStructure("true")) u_7402_1 (
    .pin10(O), .pin9(Q0), .pin8(Q1));  // open: pin1, pin2, pin3, pin4, pin5, pin6, pin13, pin12, pin11
  _7474 #(.ShowInternalStructure("true")) u_7474_1 (
    .pin1(R), .pin2(Q0), .pin3(I), .pin4(n7474_1_pin4), .pin5(Q1), .pin13(R), .pin12(O), .pin11(I),
    .pin10(n7474_1_pin10), .pin9(Q0));  // open: pin6, pin8
  // also tied to VCC on the sheet: {n7474_1_pin4, n7474_1_pin10}
endmodule

module fff4 (
  input  I,
  input  R,
  output Q1,
  output Q2,
  output Q3,
  output Q6,
  output Q9,
  output Q18,
  output Q27,
  output Q54,
  output O
);

  wire fff_1_o, fff_2_o, fff_3_o;

  fff fff_1 (.I(I), .R(R), .Q1(Q2), .Q0(Q1), .O(fff_1_o));
  fff fff_2 (.I(fff_1_o), .R(R), .Q1(Q6), .Q0(Q3), .O(fff_2_o));
  fff fff_3 (.I(fff_2_o), .R(R), .Q1(Q18), .Q0(Q9), .O(fff_3_o));
  fff fff_4 (.I(fff_3_o), .R(R), .Q1(Q54), .Q0(Q27), .O(O));
endmodule
