// Logisim project fff.circ as structural Verilog: 1 circuit, main circuit fff
module fff (
  input  I,
  input  R,
  output Q1,
  output Q0,
  output O
);

  wire n7474_1_pin4, n7474_1_pin10;

  _7402 #(.ShowInternalStructure("true")) u_7402_1 (
    .pin10(O), .pin9(Q0), .pin8(Q1));  // open: pin1, pin2, pin3, pin4, pin5, pin6, pin13, pin12, pin11
  _7474 #(.ShowInternalStructure("true")) u_7474_1 (
    .pin1(R), .pin2(Q0), .pin3(I), .pin4(n7474_1_pin4), .pin5(Q1), .pin13(R), .pin12(O), .pin11(I),
    .pin10(n7474_1_pin10), .pin9(Q0));  // open: pin6, pin8
  // also tied to VCC on the sheet: {n7474_1_pin4, n7474_1_pin10}
endmodule
