// Logisim project fff4.circ as structural Verilog: 2 circuits, main circuit fff4
module fff (
  input  I,
  input  R,
  output Q1,
  output Q0,
  output O
);

  wire n7474_1_pin4, n7474_1_pin10;

  _7402 #(.ShowInternalStructure("true")) u_7402_1 (
    .pin10(O), .pin9(Q0), .pin8(Q1));  // open: pin1, pin2, pin3, pin4, pin5, pin6, pin13, pin12, pin11
  _7474 #(.ShowInternalStructure("true")) u_7474_1 (
    .pin1(R), .pin2(Q0), .pin3(I), .pin4(n7474_1_pin4), .pin5(Q1), .pin13(R), .pin12(O), .pin11(I),
    .pin10(n7474_1_pin10), .pin9(Q0));  // open: pin6, pin8
  // also tied to VCC on the sheet: {n7474_1_pin4, n7474_1_pin10}
endmodule

module fff4 (
  input  I,
  input  R,
  output Q1,
  output Q2,
  output Q3,
  output Q6,
  output Q9,
  output Q18,
  output Q27,
  output Q54,
  output O
);

  wire fff_1_o, fff_2_o, fff_3_o;

  fff fff_1 (.I(I), .R(R), .Q1(Q2), .Q0(Q1), .O(fff_1_o));
  fff fff_2 (.I(fff_1_o), .R(R), .Q1(Q6), .Q0(Q3), .O(fff_2_o));
  fff fff_3 (.I(fff_2_o), .R(R), .Q1(Q18), .Q0(Q9), .O(fff_3_o));
  fff fff_4 (.I(fff_3_o), .R(R), .Q1(Q54), .Q0(Q27), .O(O));
endmodule
